// Logisim project aledwMIPS.circ as structural Verilog: 9 circuits, main circuit TG00MIPS
module TG00MIPS (
);

  wire clock_1_out, stopclk_1_p1, stopclk_1_p3;

  Clock #(.highDuration(2), .lowDuration(2)) clock_1 (.out(clock_1_out));
  // StopClk stopclk_1: pin names not known; wires that end beside it: stopclk_1_p1, clock_1_out, stopclk_1_p3
  MIPS mips_1 (.clk(stopclk_1_p3), .reset(1'b0), .halt(stopclk_1_p1));
endmodule

// clk
module MIPS (
  input  reset,
  input  clk,
  output halt
);

  wire alu_1_z, AluOp0, AluOp1, AluSrc, and_1_out, Branch, control_unit_1_aluop0, control_unit_1_aluop1,
       control_unit_1_alusrc, control_unit_1_branch, control_unit_1_halt, control_unit_1_jump,
       control_unit_1_memread, control_unit_1_memtoreg, control_unit_1_memwrite, control_unit_1_regdst,
       control_unit_1_regwrite, EX_2_q, EX_3_q, EX_4_q, EX_6_q, EX_7_q, EX_11_q, EX_MEM_3_q, Jump, MEM_3_q,
       MEM_5_q, MEM_6_q, MemRead, MemToReg, MemWrite, RegDst, RegWrite;
  wire [3:0] alu_control_1_out;
  wire [4:0] EX_MEM_q, ID_EX_2_q, ID_EX_3_q, instdecoder_1_rd, instdecoder_1_rs, instdecoder_1_rt,
       multiplexer_1_out, Reg2Write;
  wire [5:0] Function, instdecoder_1_funct, Opcode;
  wire [15:0] instdecoder_1_inmediate, register_1_q;
  wire [25:0] instdecoder_1_address;
  wire [27:0] bit_extender_1_out, shifter_1_out;
  wire [31:0] adder_2_out, alu_1_result, bit_extender_2_out, data_memory_32_1_read_data, EX_MEM_2_q,
       EX_MEM_4_q, EX_MEM_5_q, ID_EX_4_q, ID_EX_5_q, ID_EX_6_q, ID_EX_7_q, IF_ID_2_q, IF_ID_q,
       instruction_memory_1_instruction, MEM_WB_2_q, MEM_WB_3_q, multiplexer_2_out, multiplexer_3_out,
       multiplexer_5_out, PC_1, PC_q, register_file_1_read_data_1, register_file_1_read_data_2, Send_to_PC,
       shifter_2_out;

  Register #(.width(32)) PC (.D(Send_to_PC), .Q(PC_q), .clk(clk), .clr(reset));  // open: en
  Control_Unit control_unit_1 (
    .in_1(Opcode), .AluOp0(control_unit_1_aluop0), .AluOp1(control_unit_1_aluop1),
    .RegDst(control_unit_1_regdst), .RegWrite(control_unit_1_regwrite), .ALUSrc(control_unit_1_alusrc),
    .MemWrite(control_unit_1_memwrite), .MemRead(control_unit_1_memread), .MemtoReg(control_unit_1_memtoreg),
    .Branch(control_unit_1_branch), .Jump(control_unit_1_jump), .Halt(control_unit_1_halt));
  Register #(.width(1), .trigger("falling")) EX (.D(control_unit_1_aluop0), .Q(AluOp0), .clk(clk));  // open: en, clr
  Register #(.width(1), .trigger("falling")) EX_2 (.D(control_unit_1_memread), .Q(EX_2_q), .clk(clk));  // open: en, clr
  Register #(.width(1), .trigger("falling")) EX_3 (
    .D(control_unit_1_memtoreg), .Q(EX_3_q), .clk(clk));  // open: en, clr
  Register #(.width(1), .trigger("falling")) EX_4 (.D(control_unit_1_branch), .Q(EX_4_q), .clk(clk));  // open: en, clr
  Register #(.width(1), .trigger("falling")) EX_5 (.D(control_unit_1_jump), .Q(Jump), .clk(clk));  // open: en, clr
  Register #(.width(1), .trigger("falling")) EX_6 (.D(control_unit_1_halt), .Q(EX_6_q), .clk(clk));  // open: en, clr
  Register #(.width(1), .trigger("falling")) EX_7 (
    .D(control_unit_1_regwrite), .Q(EX_7_q), .clk(clk));  // open: en, clr
  Adder #(.width(32)) adder_1 (.a(PC_q), .b(32'h4), .out(PC_1));  // open: cin, cout
  Instruction_memory instruction_memory_1 (.Read_address(PC_q), .Instruction(instruction_memory_1_instruction));
  Register #(.width(1), .trigger("falling")) EX_8 (.D(control_unit_1_aluop1), .Q(AluOp1), .clk(clk));  // open: en, clr
  Register #(.width(1), .trigger("falling")) EX_9 (.D(control_unit_1_regdst), .Q(RegDst), .clk(clk));  // open: en, clr
  Register #(.width(1), .trigger("falling")) EX_10 (.D(control_unit_1_alusrc), .Q(AluSrc), .clk(clk));  // open: en, clr
  Register #(.width(1), .trigger("falling")) MEM (.D(EX_11_q), .Q(MemWrite), .clk(clk));  // open: en, clr
  Register #(.width(1), .trigger("falling")) EX_11 (
    .D(control_unit_1_memwrite), .Q(EX_11_q), .clk(clk));  // open: en, clr
  Register #(.width(1), .trigger("falling")) MEM_2 (.D(EX_2_q), .Q(MemRead), .clk(clk));  // open: en, clr
  Register #(.width(1), .trigger("falling")) MEM_3 (.D(EX_3_q), .Q(MEM_3_q), .clk(clk));  // open: en, clr
  Register #(.width(1), .trigger("falling")) MEM_4 (.D(EX_4_q), .Q(Branch), .clk(clk));  // open: en, clr
  Register #(.width(1), .trigger("falling")) MEM_5 (.D(EX_6_q), .Q(MEM_5_q), .clk(clk));  // open: en, clr
  Register #(.width(1), .trigger("falling")) MEM_6 (.D(EX_7_q), .Q(MEM_6_q), .clk(clk));  // open: en, clr
  Register #(.width(1), .trigger("falling")) WB (.D(MEM_6_q), .Q(RegWrite), .clk(clk));  // open: en, clr
  // Probe on instruction_memory_1_instruction
  Register #(.width(1), .trigger("falling")) WB_2 (.D(MEM_3_q), .Q(MemToReg), .clk(clk));  // open: en, clr
  Register #(.width(1), .trigger("falling")) WB_3 (.D(MEM_5_q), .Q(halt), .clk(clk));  // open: en, clr
  assign bit_extender_1_out = {{2{instdecoder_1_address[25]}}, instdecoder_1_address};  // Bit_Extender bit_extender_1
  Register #(.width(32), .trigger("falling")) IF_ID (
    .D(instruction_memory_1_instruction), .Q(IF_ID_q), .clk(clk));  // open: en, clr
  InstDecoder instdecoder_1 (
    .instruction(IF_ID_q), .OPCODE(Opcode), .RS(instdecoder_1_rs), .RT(instdecoder_1_rt),
    .RD(instdecoder_1_rd), .FUNCT(instdecoder_1_funct), .INMEDIATE(instdecoder_1_inmediate),
    .ADDRESS(instdecoder_1_address));
  Register #(.width(6), .trigger("falling")) ID_EX (.D(instdecoder_1_funct), .Q(Function), .clk(clk));  // open: en, clr
  Shifter #(.width(28)) shifter_1 (.in(bit_extender_1_out), .\dist (5'b00010), .out(shifter_1_out));
  Register #(.width(32), .trigger("falling")) IF_ID_2 (.D(PC_1), .Q(IF_ID_2_q), .clk(clk));  // open: en, clr
  // Probe on multiplexer_5_out
  Register #(.width(16), .trigger("falling")) register_1 (
    .D(instdecoder_1_inmediate), .Q(register_1_q), .clk(clk));  // open: en, clr
  Register #(.width(5), .trigger("falling")) ID_EX_2 (.D(instdecoder_1_rt), .Q(ID_EX_2_q), .clk(clk));  // open: en, clr
  Register #(.width(5), .trigger("falling")) ID_EX_3 (.D(instdecoder_1_rd), .Q(ID_EX_3_q), .clk(clk));  // open: en, clr
  Register_file register_file_1 (
    .Read_Register_1(instdecoder_1_rs), .Read_Register_2(instdecoder_1_rt), .Write_Register(Reg2Write),
    .Write_Data(multiplexer_5_out), .Read_Data_1(register_file_1_read_data_1),
    .Read_Data_2(register_file_1_read_data_2), .clk(clk), .reset(reset), .Write(RegWrite));
  Register #(.width(32), .trigger("falling")) ID_EX_4 (
    .D(register_file_1_read_data_1), .Q(ID_EX_4_q), .clk(clk));  // open: en, clr
  Register #(.width(32), .trigger("falling")) ID_EX_5 (
    .D(register_file_1_read_data_2), .Q(ID_EX_5_q), .clk(clk));  // open: en, clr
  Register #(.width(32), .trigger("falling")) ID_EX_6 (
    .D({IF_ID_2_q[31:28], shifter_1_out}), .Q(ID_EX_6_q), .clk(clk));  // open: en, clr
  assign bit_extender_2_out = {{16{register_1_q[15]}}, register_1_q};  // Bit_Extender bit_extender_2
  Multiplexer #(.width(5)) multiplexer_1 (
    .in0(ID_EX_2_q), .in1(ID_EX_3_q), .out(multiplexer_1_out), .sel(RegDst));  // open: en
  Register #(.width(32), .trigger("falling")) ID_EX_7 (.D(IF_ID_2_q), .Q(ID_EX_7_q), .clk(clk));  // open: en, clr
  Shifter #(.width(32)) shifter_2 (.in(bit_extender_2_out), .\dist (5'b00010), .out(shifter_2_out));
  Register #(.width(5), .trigger("falling")) EX_MEM (.D(multiplexer_1_out), .Q(EX_MEM_q), .clk(clk));  // open: en, clr
  Alu_Control alu_control_1 (
    .AluOp1(AluOp0), .AluOP0(AluOp1), .Function(Function), .OUT(alu_control_1_out));  // open: Op0, Op1, Op2, Op3
  Multiplexer #(.width(32), .enable("false")) multiplexer_2 (
    .in0(ID_EX_5_q), .in1(bit_extender_2_out), .out(multiplexer_2_out), .sel(AluSrc));
  Register #(.width(32), .trigger("falling")) EX_MEM_2 (.D(adder_2_out), .Q(EX_MEM_2_q), .clk(clk));  // open: en, clr
  Adder #(.width(32)) adder_2 (.a(ID_EX_7_q), .b(shifter_2_out), .out(adder_2_out));  // open: cin, cout
  and and_1 (and_1_out, Branch, EX_MEM_3_q);
  Multiplexer #(.width(32), .enable("false")) multiplexer_3 (
    .in0(PC_1), .in1(EX_MEM_2_q), .out(multiplexer_3_out), .sel(and_1_out));
  ALU alu_1 (.A(ID_EX_4_q), .B(multiplexer_2_out), .Z(alu_1_z), .Result(alu_1_result), .Operation(alu_control_1_out));
  Register #(.width(5), .trigger("falling")) MEM_WB (.D(EX_MEM_q), .Q(Reg2Write), .clk(clk));  // open: en, clr
  Multiplexer #(.width(32), .enable("false")) multiplexer_4 (
    .in0(multiplexer_3_out), .in1(ID_EX_6_q), .out(Send_to_PC), .sel(Jump));
  Register #(.width(1), .trigger("falling")) EX_MEM_3 (.D(alu_1_z), .Q(EX_MEM_3_q), .clk(clk));  // open: en, clr
  Register #(.width(32), .trigger("falling")) EX_MEM_4 (.D(alu_1_result), .Q(EX_MEM_4_q), .clk(clk));  // open: en, clr
  Register #(.width(32), .trigger("falling")) EX_MEM_5 (.D(ID_EX_5_q), .Q(EX_MEM_5_q), .clk(clk));  // open: en, clr
  Data_Memory_32 data_memory_32_1 (
    .Address(EX_MEM_4_q), .Write_Data(EX_MEM_5_q), .Read_Data(data_memory_32_1_read_data), .Write(MemWrite),
    .clk(clk), .reset(reset), .Read(MemRead));
  Register #(.width(32), .trigger("falling")) MEM_WB_2 (.D(EX_MEM_4_q), .Q(MEM_WB_2_q), .clk(clk));  // open: en, clr
  Register #(.width(32), .trigger("falling")) MEM_WB_3 (
    .D(data_memory_32_1_read_data), .Q(MEM_WB_3_q), .clk(clk), .clr(clk));  // open: en
  Multiplexer #(.width(32), .enable("false")) multiplexer_5 (
    .in0(MEM_WB_2_q), .in1(MEM_WB_3_q), .out(multiplexer_5_out), .sel(MemToReg));
endmodule

module Register_file (
  input  clk,
  input  reset,
  input  [4:0] Read_Register_1,
  input  [4:0] Read_Register_2,
  input  [4:0] Write_Register,
  input  [31:0] Write_Data,
  input  Write,
  output [31:0] Read_Data_1,
  output [31:0] Read_Data_2
);

  wire decoder_1_out1, decoder_1_out2, decoder_1_out3, decoder_1_out4, decoder_1_out5, decoder_1_out6,
       decoder_1_out7, decoder_1_out8, decoder_1_out9, decoder_1_out10, decoder_1_out11, decoder_1_out12,
       decoder_1_out13, decoder_1_out14, decoder_1_out15, decoder_1_out16, decoder_1_out17, decoder_1_out18,
       decoder_1_out19, decoder_1_out20, decoder_1_out21, decoder_1_out22, decoder_1_out23, decoder_1_out24,
       decoder_1_out25, decoder_1_out26, decoder_1_out27, decoder_1_out28, decoder_1_out29, decoder_1_out30,
       decoder_1_out31;
  wire [31:0] delayer1x32_1_p2, multiplexer_1_out, multiplexer_2_out, R1_q, R2_q, R3_q, R4_q, R5_q, R6_q,
       R7_q, R8_q, R9_q, R10_q, R11_q, R12_q, R13_q, R14_q, R15_q, R16_q, R17_q, R18_q, R19_q, R20_q, R21_q,
       R22_q, R23_q, R24_q, R25_q, R26_q, R27_q, R28_q, R29_q, R30_q, R31_q;

  Decoder #(.select(5), .disabled(0)) decoder_1 (
    .out1(decoder_1_out1), .out2(decoder_1_out2), .out3(decoder_1_out3), .out4(decoder_1_out4),
    .out5(decoder_1_out5), .out6(decoder_1_out6), .out7(decoder_1_out7), .out8(decoder_1_out8),
    .out9(decoder_1_out9), .out10(decoder_1_out10), .out11(decoder_1_out11), .out12(decoder_1_out12),
    .out13(decoder_1_out13), .out14(decoder_1_out14), .out15(decoder_1_out15), .out16(decoder_1_out16),
    .out17(decoder_1_out17), .out18(decoder_1_out18), .out19(decoder_1_out19), .out20(decoder_1_out20),
    .out21(decoder_1_out21), .out22(decoder_1_out22), .out23(decoder_1_out23), .out24(decoder_1_out24),
    .out25(decoder_1_out25), .out26(decoder_1_out26), .out27(decoder_1_out27), .out28(decoder_1_out28),
    .out29(decoder_1_out29), .out30(decoder_1_out30), .out31(decoder_1_out31), .sel(Write_Register),
    .en(Write));  // open: out0
  // Delayer1x32 delayer1x32_1: pin names not known; wires that end beside it: Write_Data, delayer1x32_1_p2
  Register #(.width(32)) R1 (.D(delayer1x32_1_p2), .en(decoder_1_out1), .Q(R1_q), .clk(clk), .clr(reset));
  Register #(.width(32)) R2 (.D(delayer1x32_1_p2), .en(decoder_1_out2), .Q(R2_q), .clk(clk), .clr(reset));
  Register #(.width(32)) R3 (.D(delayer1x32_1_p2), .en(decoder_1_out3), .Q(R3_q), .clk(clk), .clr(reset));
  Register #(.width(32)) R4 (.D(delayer1x32_1_p2), .en(decoder_1_out4), .Q(R4_q), .clk(clk), .clr(reset));
  Register #(.width(32)) R5 (.D(delayer1x32_1_p2), .en(decoder_1_out5), .Q(R5_q), .clk(clk), .clr(reset));
  Register #(.width(32)) R6 (.D(delayer1x32_1_p2), .en(decoder_1_out6), .Q(R6_q), .clk(clk), .clr(reset));
  Register #(.width(32)) R7 (.D(delayer1x32_1_p2), .en(decoder_1_out7), .Q(R7_q), .clk(clk), .clr(reset));
  Register #(.width(32)) R8 (.D(delayer1x32_1_p2), .en(decoder_1_out8), .Q(R8_q), .clk(clk), .clr(reset));
  Register #(.width(32)) R9 (.D(delayer1x32_1_p2), .en(decoder_1_out9), .Q(R9_q), .clk(clk), .clr(reset));
  Register #(.width(32)) R10 (.D(delayer1x32_1_p2), .en(decoder_1_out10), .Q(R10_q), .clk(clk), .clr(reset));
  Register #(.width(32)) R11 (.D(delayer1x32_1_p2), .en(decoder_1_out11), .Q(R11_q), .clk(clk), .clr(reset));
  Register #(.width(32)) R12 (.D(delayer1x32_1_p2), .en(decoder_1_out12), .Q(R12_q), .clk(clk), .clr(reset));
  Register #(.width(32)) R13 (.D(delayer1x32_1_p2), .en(decoder_1_out13), .Q(R13_q), .clk(clk), .clr(reset));
  Register #(.width(32)) R14 (.D(delayer1x32_1_p2), .en(decoder_1_out14), .Q(R14_q), .clk(clk), .clr(reset));
  Register #(.width(32)) R15 (.D(delayer1x32_1_p2), .en(decoder_1_out15), .Q(R15_q), .clk(clk), .clr(reset));
  Register #(.width(32)) R16 (.D(delayer1x32_1_p2), .en(decoder_1_out16), .Q(R16_q), .clk(clk), .clr(reset));
  Register #(.width(32)) R17 (.D(delayer1x32_1_p2), .en(decoder_1_out17), .Q(R17_q), .clk(clk), .clr(reset));
  Register #(.width(32)) R18 (.D(delayer1x32_1_p2), .en(decoder_1_out18), .Q(R18_q), .clk(clk), .clr(reset));
  Register #(.width(32)) R19 (.D(delayer1x32_1_p2), .en(decoder_1_out19), .Q(R19_q), .clk(clk), .clr(reset));
  Register #(.width(32)) R20 (.D(delayer1x32_1_p2), .en(decoder_1_out20), .Q(R20_q), .clk(clk), .clr(reset));
  Register #(.width(32)) R21 (.D(delayer1x32_1_p2), .en(decoder_1_out21), .Q(R21_q), .clk(clk), .clr(reset));
  Register #(.width(32)) R22 (.D(delayer1x32_1_p2), .en(decoder_1_out22), .Q(R22_q), .clk(clk), .clr(reset));
  Register #(.width(32)) R23 (.D(delayer1x32_1_p2), .en(decoder_1_out23), .Q(R23_q), .clk(clk), .clr(reset));
  Register #(.width(32)) R24 (.D(delayer1x32_1_p2), .en(decoder_1_out24), .Q(R24_q), .clk(clk), .clr(reset));
  Register #(.width(32)) R25 (.D(delayer1x32_1_p2), .en(decoder_1_out25), .Q(R25_q), .clk(clk), .clr(reset));
  Register #(.width(32)) R26 (.D(delayer1x32_1_p2), .en(decoder_1_out26), .Q(R26_q), .clk(clk), .clr(reset));
  Register #(.width(32)) R27 (.D(delayer1x32_1_p2), .en(decoder_1_out27), .Q(R27_q), .clk(clk), .clr(reset));
  Register #(.width(32)) R28 (.D(delayer1x32_1_p2), .en(decoder_1_out28), .Q(R28_q), .clk(clk), .clr(reset));
  Register #(.width(32)) R29 (.D(delayer1x32_1_p2), .en(decoder_1_out29), .Q(R29_q), .clk(clk), .clr(reset));
  Register #(.width(32)) R30 (.D(delayer1x32_1_p2), .en(decoder_1_out30), .Q(R30_q), .clk(clk), .clr(reset));
  Register #(.width(32)) R31 (.D(delayer1x32_1_p2), .en(decoder_1_out31), .Q(R31_q), .clk(clk), .clr(reset));
  Multiplexer #(.select(5), .width(32), .enable("false")) multiplexer_1 (
    .in0({32{1'b0}}), .in1(R1_q), .in2(R2_q), .in3(R3_q), .in4(R4_q), .in5(R5_q), .in6(R6_q), .in7(R7_q),
    .in8(R8_q), .in9(R9_q), .in10(R10_q), .in11(R11_q), .in12(R12_q), .in13(R13_q), .in14(R14_q),
    .in15(R15_q), .in16(R16_q), .in17(R17_q), .in18(R18_q), .in19(R19_q), .in20(R20_q), .in21(R21_q),
    .in22(R22_q), .in23(R23_q), .in24(R24_q), .in25(R25_q), .in26(R26_q), .in27(R27_q), .in28(R28_q),
    .in29(R29_q), .in30(R30_q), .in31(R31_q), .out(multiplexer_1_out), .sel(Read_Register_1));
  Multiplexer #(.select(5), .width(32), .enable("false")) multiplexer_2 (
    .in0({32{1'b0}}), .in1(R1_q), .in2(R2_q), .in3(R3_q), .in4(R4_q), .in5(R5_q), .in6(R6_q), .in7(R7_q),
    .in8(R8_q), .in9(R9_q), .in10(R10_q), .in11(R11_q), .in12(R12_q), .in13(R13_q), .in14(R14_q),
    .in15(R15_q), .in16(R16_q), .in17(R17_q), .in18(R18_q), .in19(R19_q), .in20(R20_q), .in21(R21_q),
    .in22(R22_q), .in23(R23_q), .in24(R24_q), .in25(R25_q), .in26(R26_q), .in27(R27_q), .in28(R28_q),
    .in29(R29_q), .in30(R30_q), .in31(R31_q), .out(multiplexer_2_out), .sel(Read_Register_2));
  // Delayer1x32 delayer1x32_2: pin names not known; wires that end beside it: multiplexer_1_out, Read_Data_1
  // Delayer1x32 delayer1x32_3: pin names not known; wires that end beside it: multiplexer_2_out, Read_Data_2
endmodule

module ALU (
  input  [3:0] Operation,
  input  [31:0] A,
  input  [31:0] B,
  output Z,
  output [31:0] Result
);

  wire nor_1_out;
  wire [0:0] comparator_1_lt;
  wire [31:0] adder_1_out, and_1_out, multiplexer_1_out, multiplexer_2_out, multiplexer_3_out, not_1_out,
       not_2_out, or_1_out;

  assign not_1_out = ~A;  // NOT_Gate not_1, 32 bits wide
  assign not_2_out = ~B;  // NOT_Gate not_2, 32 bits wide
  Comparator #(.width(32)) comparator_1 (.a(A), .b(B), .lt(comparator_1_lt[0]));  // open: gt, eq
  Multiplexer #(.width(32), .enable("false")) multiplexer_1 (
    .in0(A), .in1(not_1_out), .out(multiplexer_1_out), .sel(Operation[3]));
  Multiplexer #(.width(32), .enable("false")) multiplexer_2 (
    .in0(B), .in1(not_2_out), .out(multiplexer_2_out), .sel(Operation[2]));
  assign and_1_out = multiplexer_1_out & multiplexer_2_out;  // AND_Gate and_1, 32 bits wide
  assign or_1_out = multiplexer_1_out | multiplexer_2_out;  // OR_Gate or_1, 32 bits wide
  Adder #(.width(32)) adder_1 (
    .a(multiplexer_1_out), .b(multiplexer_2_out), .out(adder_1_out), .cin(Operation[2]));  // open: cout
  Multiplexer #(.select(2), .width(32), .enable("false")) multiplexer_3 (
    .in0(and_1_out), .in1(or_1_out), .in2(adder_1_out), .in3({{31{1'b0}}, comparator_1_lt[0]}),
    .out(multiplexer_3_out), .sel(Operation[1:0]));
  nor nor_1 (nor_1_out, multiplexer_3_out[0], multiplexer_3_out[1], multiplexer_3_out[2], multiplexer_3_out[3], multiplexer_3_out[4], multiplexer_3_out[5], multiplexer_3_out[6], multiplexer_3_out[7], multiplexer_3_out[8], multiplexer_3_out[9], multiplexer_3_out[10], multiplexer_3_out[11], multiplexer_3_out[12], multiplexer_3_out[13], multiplexer_3_out[14], multiplexer_3_out[15], multiplexer_3_out[16], multiplexer_3_out[17], multiplexer_3_out[18], multiplexer_3_out[19], multiplexer_3_out[20], multiplexer_3_out[21], multiplexer_3_out[22], multiplexer_3_out[23], multiplexer_3_out[24], multiplexer_3_out[25], multiplexer_3_out[26], multiplexer_3_out[27], multiplexer_3_out[28], multiplexer_3_out[29], multiplexer_3_out[30], multiplexer_3_out[31]);
  // Delayer2x32 delayer2x32_1: pin names not known; wires that end beside it: multiplexer_3_out, Result
  // Delayer2x1 delayer2x1_1: pin names not known; wires that end beside it: nor_1_out, Z

  // Notes on the sheet:
  //   0001    OR
  //   Operation    Function
  //   0000    AND
  //   0010    add
  //   0110    subtract
  //   0111    set on less than
  //   1100    NOR
endmodule

module Data_Memory_32 (
  input  Write,
  input  [31:0] Address,
  input  [31:0] Write_Data,
  input  clk,
  input  reset,
  input  Read,
  output [31:0] Read_Data
);

  wire [9:0] bitselector_1_out;
  wire [31:0] delayer2x32_1_p2, ram_1_data;

  BitSelector #(.width(32), .group(10)) bitselector_1 (.in(Address), .out(bitselector_1_out), .sel(2'b00));
  // Delayer2x32 delayer2x32_1: pin names not known; wires that end beside it: Write_Data, delayer2x32_1_p2
  RAM #(.dataWidth(32), .bus("separate"), .Datafile_on_reset("TG00ram.txt")) ram_1 (
    .addr(bitselector_1_out[9:2]), .din(delayer2x32_1_p2), .data(ram_1_data), .str(Write), .sel(1'b1),
    .clk(clk), .ld(Read), .clr(reset));
  // Delayer2x32 delayer2x32_2: pin names not known; wires that end beside it: ram_1_data, Read_Data

  // Notes on the sheet:
  //   Memoria de 32 bits direccionable a nivel de byte
  //   Tan solo implementadas las 256 primeras posiciones de 32 bits o 1024 bytes
endmodule

module Instruction_memory (
  input  [31:0] Read_address,
  output [31:0] Instruction
);

  wire [6:0] bitselector_1_out;
  wire [31:0] ram_1_data;

  BitSelector #(.width(30), .group(7)) bitselector_1 (.in(Read_address[31:2]), .out(bitselector_1_out), .sel(3'b000));
  RAM #(.addrWidth(7), .dataWidth(32), .bus("asynch"), .Datafile_on_reset("TG00rom.txt")) ram_1 (
    .addr(bitselector_1_out), .data(ram_1_data), .sel(1'b1), .ld(1'b1), .clr(1'b0));
  // Delayer2x32 delayer2x32_1: pin names not known; wires that end beside it: ram_1_data, Instruction
endmodule

module InstDecoder (
  input  [31:0] instruction,
  output [5:0] OPCODE,
  output [4:0] RS,
  output [4:0] RT,
  output [4:0] RD,
  output [5:0] FUNCT,
  output [15:0] INMEDIATE,
  output [25:0] ADDRESS
);


  assign ADDRESS = instruction[25:0];
  assign FUNCT = instruction[5:0];
  assign INMEDIATE = instruction[15:0];
  assign OPCODE = instruction[31:26];
  assign RD = instruction[15:11];
  assign RS = instruction[25:21];
  assign RT = instruction[20:16];
endmodule

module Control_Unit (
  input  [5:0] in_1,
  output AluOp0,
  output AluOp1,
  output RegDst,
  output RegWrite,
  output ALUSrc,
  output MemWrite,
  output MemRead,
  output MemtoReg,
  output Branch,
  output Jump,
  output Halt
);

  and R_Type (AluOp0, ~in_1[0], ~in_1[1], ~in_1[2], ~in_1[3], ~in_1[4], ~in_1[5]);  // AND_Gate
  and Load (MemRead, in_1[0], in_1[1], ~in_1[2], ~in_1[3], ~in_1[4], in_1[5]);  // AND_Gate
  and Store (MemWrite, in_1[0], in_1[1], ~in_1[2], in_1[3], ~in_1[4], in_1[5]);  // AND_Gate
  and beq (AluOp1, ~in_1[0], ~in_1[1], in_1[2], ~in_1[3], ~in_1[4], ~in_1[5]);  // AND_Gate
  and u_jump (Jump, ~in_1[0], in_1[1], ~in_1[2], ~in_1[3], ~in_1[4], ~in_1[5]);  // AND_Gate
  and u_Halt (Halt, in_1[0], in_1[1], in_1[2], in_1[3], in_1[4], in_1[5]);
  and and_1 (RegDst, ~MemRead, AluOp0);  // AND_Gate
  or or_1 (RegWrite, MemRead, AluOp0);
  or or_2 (ALUSrc, MemRead, MemWrite);

  assign Branch = AluOp1;
  assign MemtoReg = MemRead;

  // Other names for the same wires on the sheet: beq = AluOp1; Load = MemRead; R_Type = AluOp0; Store = MemWrite
endmodule

module Alu_Control (
  input  AluOp1,
  input  AluOP0,
  input  [5:0] Function,
  output Op0,
  output Op1,
  output [3:0] OUT,
  output Op2,
  output Op3
);

  wire and_1_out, or_1_out;

  or or_1 (or_1_out, Function[0], Function[3]);
  and and_1 (and_1_out, AluOp1, Function[1]);
  and and_2 (Op0, AluOp1, or_1_out);
  or or_2 (Op1, ~AluOp1, ~Function[2]);  // OR_Gate
  or or_3 (Op2, AluOP0, and_1_out);

  assign Op3 = 1'b0;
  assign OUT = {1'b0, Op2, Op1, Op0};
endmodule
