// Logisim project Multiplexor 2 entries.circ as structural Verilog: 2 circuits, main circuit main
module main (
  input  in_1,
  input  in_2,
  input  Chipset,
  output Out
);

  wire and_1_out, and_2_out, not_1_out;

  and and_1 (and_1_out, in_1, not_1_out);
  not not_1 (not_1_out, Chipset);
  and and_2 (and_2_out, in_2, Chipset);
  or or_1 (Out, and_1_out, and_2_out);
endmodule

module _4_1_MUX (
  input  in_1,
  input  in_2,
  input  in_3,
  input  in_4,
  input  in_5,
  input  in_6,
  output out_7
);

  wire main_1_out, main_2_out;

  main main_1 (.in_1(in_1), .in_2(in_2), .Chipset(in_6), .Out(main_1_out));
  main main_2 (.in_1(in_3), .in_2(in_4), .Chipset(in_6), .Out(main_2_out));
  main main_3 (.in_1(main_1_out), .in_2(main_2_out), .Chipset(in_5), .Out(out_7));
endmodule
