// Logisim project Xor Circuit Built Using Logisim.circ as structural Verilog: 2 circuits, main circuit main
module main (
  input  Y,
  input  X,
  output Output
);

  wire and_1_out, and_2_out, not_1_out, not_2_out;

  not not_1 (not_1_out, Y);
  not not_2 (not_2_out, X);
  MUX_2_1 mux_2_1_1 ();  // open: in_1, in_2, Chipset, Out
  and and_1 (and_1_out, not_1_out, X);
  and and_2 (and_2_out, Y, not_2_out);
  or or_1 (Output, and_1_out, and_2_out);

  // Notes on the sheet:
  //   XOR Circuit built using Logism
endmodule

module MUX_2_1 (
  input  in_1,
  input  in_2,
  input  Chipset,
  output Out
);

  wire and_1_out, and_2_out, not_1_out;

  and and_1 (and_1_out, in_1, not_1_out);
  not not_1 (not_1_out, Chipset);
  and and_2 (and_2_out, in_2, Chipset);
  or or_1 (Out, and_1_out, and_2_out);
endmodule
